# Fritzing sketch wiring diagram (saved by Fritzing 0.9.3b)

parts:
  Bauteil1 = NeoPixel Stick [part_number=1426]
  Bauteil2 = NeoPixel Stick [part_number=1426]
  Bauteil3 = Arduino Nano (Rev3.0) (ICSP)

nets:
  GND: Bauteil1.GND, Bauteil2.GND, Bauteil3.GND
  N1: Bauteil1.DATAOUT, Bauteil2.DATAIN
  +5V: Bauteil1.+5V, Bauteil2.+5V, Bauteil3.5V
  N2: Bauteil1.DATAIN, Bauteil3.D6

custom parts:
  NeoPixel Stick: Make your own little LED strip arrangement with this stick of NeoPixel LEDs. We crammed 8 of the tiny 5050 (5mm x 5mm) smart RGB LEDs onto a PCB with mounting holes and a chainable design. Use only one microcontroller pin to control as many as you can chain together! Each LED is addressable as the driver chip is inside the LED. Each one has ~18mA constant current drive so the color will be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
